// Logisim project MyCPU.circ as structural Verilog: 2 circuits, main circuit main
module main (
  input  in_1,
  input  in_2,
  output out_3
);

  and and_1 (out_3, in_1, in_2);
  Transistor transistor_1 ();  // open: in, out, gate
endmodule

module ULA (
  input  [15:0] A,
  input  [15:0] B,
  input  [3:0] op,
  output [15:0] out_4
);

  wire OutBg, OutEq, OutSm;
  wire [15:0] OutAnd, OutDiv, OutMul, OutNot, OutOr, OutSub, OutSum, OutXor;

  Adder #(.width(16)) adder_1 (.a(A), .b(B), .out(OutSum));  // open: cin, cout
  Subtractor #(.width(16)) subtractor_1 (.a(A), .b(B), .out(OutSub));  // open: bin, bout
  Multiplier #(.width(16)) multiplier_1 (.a(A), .b(B), .out(OutMul));  // open: cin, cout
  Divider #(.width(16)) divider_1 (.a(A), .b(B), .out(OutDiv));  // open: upper, rem
  Comparator #(.width(16)) comparator_1 (.a(A), .b(B), .gt(OutBg), .eq(OutEq), .lt(OutSm));
  assign OutAnd = A & B;  // AND_Gate and_1, 16 bits wide
  assign OutOr = A | B;  // OR_Gate or_1, 16 bits wide
  assign OutNot = ~A;  // NOT_Gate not_1, 16 bits wide
  assign OutXor = A ^ B;  // XOR_Gate xor_1, 16 bits wide
  Multiplexer #(.select(4), .width(16)) multiplexer_1 (.out(out_4));  // open: in0, in1, in2, in3, in4, in5, in6, in7, in8, in9, in10, in11, in12, in13, in14, in15, sel, en

  // Other names for the same wires on the sheet: Output[15:0] = out_4
endmodule
